// Logisim project ld.circ as structural Verilog: 1 circuit, main circuit main
module main (
  input  A,
  input  B,
  input  C,
  input  D,
  output a_2,
  output b_2,
  output c_2,
  output d_2,
  output e,
  output f,
  output f_2
);

  wire and_1_out, and_2_out, and_3_out, and_4_out, and_5_out, and_6_out, and_7_out, and_8_out, and_9_out,
       and_10_out, and_12_out, and_13_out, and_14_out, and_15_out, and_16_out, not_1_out, not_2_out,
       not_3_out;

  not not_1 (not_1_out, B);
  not not_2 (not_2_out, C);
  not not_3 (not_3_out, B);
  and and_1 (and_1_out, B, not_2_out);
  and and_2 (and_2_out, not_3_out, C);
  and and_3 (and_3_out, not_1_out, C);
  and and_4 (and_4_out, not_1_out, not_3_out);
  and and_5 (and_5_out, B, B);
  and and_6 (and_6_out, not_2_out, not_3_out);
  and and_7 (and_7_out, C, B);
  or or_1 (b_2, and_6_out, and_7_out, not_1_out);
  or or_2 (f_2, and_1_out, A, and_2_out, and_3_out);
  or or_3 (a_2, C, and_4_out, and_5_out, A);
  or or_4 (c_2, B, B, not_2_out);
  and and_8 (and_8_out, B, B, not_2_out);
  and and_9 (and_9_out, C, not_3_out);
  and and_10 (and_10_out, not_1_out, not_3_out);
  and and_11 (and_9_out, not_1_out, C);
  or or_5 (d_2, and_9_out, and_8_out, A, and_9_out, and_10_out);
  and and_12 (and_12_out, not_1_out, C);
  and and_13 (and_13_out, not_1_out, not_3_out);
  or or_6 (e, and_12_out, and_13_out);
  and and_14 (and_14_out, not_2_out, B);
  and and_15 (and_15_out, not_2_out, not_3_out);
  and and_16 (and_16_out, not_3_out, B);
  or or_7 (f, A, and_16_out, and_14_out, and_15_out);

  assign D = B;
endmodule
